// Logisim project LAB - 4.circ as structural Verilog: 4 circuits, main circuit main
module main (
  input  A,
  input  B,
  output X
);

  wire and_1_out, and_2_out;

  and and_1 (and_1_out, A, B);
  and and_2 (and_2_out, A, ~B);  // AND_Gate
  or or_1 (X, and_1_out, and_2_out);

  // Notes on the sheet:
  //   Kieran O'Connor
endmodule

module Lab_4_Karnaugh_map (
  input  A,
  input  B,
  input  C,
  input  D,
  output out_5
);

  wire and_1_out, and_2_out, and_3_out;

  and and_1 (and_1_out, ~A, ~C);  // AND_Gate
  and and_2 (and_2_out, ~B, ~C, D);  // AND_Gate
  and and_3 (and_3_out, A, B, C);
  or or_1 (out_5, and_1_out, and_2_out, and_3_out);

  // Notes on the sheet:
  //   Kieran O'Connor
endmodule

module mux (
  input  D0,
  input  D1,
  input  S,
  output Y
);

  wire and_1_out, and_2_out;

  and and_1 (and_1_out, D0, ~S);  // AND_Gate
  and and_2 (and_2_out, D1, S);
  or or_1 (Y, and_1_out, and_2_out);

  // Notes on the sheet:
  //   Kieran O'Connor
endmodule

module Decoder (
  input  A,
  input  B,
  output out_3,
  output out_4,
  output out_5,
  output out_6
);

  and and_1 (out_3, ~A, ~B);  // AND_Gate
  and and_2 (out_4, ~A, B);  // AND_Gate
  and and_3 (out_5, A, ~B);  // AND_Gate
  and and_4 (out_6, A, B);

  // Notes on the sheet:
  //   Kieran O'Connor
endmodule
